# Fritzing sketch FeatherWingTFT (saved by Fritzing 0.9.6b)

parts:
  Part1 = Adafruit 3.5in 480x320 TFT FeatherWing [part_number="Adafrruit #3651"]
  Part2 = Adafruit ESP32-S3 Feather [part_number="Adafruit #5323"]
  Part3 = Adafruit DC+Stepper FeatherWing [part_number="Adafruit #2927"]
  Part4 = Adafruit FeatherWing Proto [part_number="Adafruit #2884"]
  J1 = male pin header, 3 pins [form="♂ (male)"]

nets:
  N1: Part1.!RESET, Part2.RESET, Part3.RESET
  3.3V: Part1.3.3V, Part1.AREF, Part2.3.3V, Part3.AREF, Part3.+3.3V
  GND: Part1.GND, Part2.GND, Part3.GND
  N2: Part1.A, Part2.A0, Part3.A
  N3: Part1.B, Part2.A1, Part3.B
  N4: Part1.C, Part2.A2, Part3.C
  N5: Part1.D, Part2.A3, Part3.D
  N6: Part1.E, Part2.A4, Part3.E
  N7: Part1.F, Part2.A5, Part3.F
  N8: Part1.SCLK, Part2.SCK, Part3.SCK
  N9: Part1.MOSI, Part2.MOSI, Part3.MOSI
  N10: Part1.MISO, Part2.MISO, Part3.MISO
  N11: Part1.RX, Part2.RX, Part3.RX
  N12: Part1.TX, Part2.TX, Part3.TX
  N13: Part1.G, Part2.TXD0, Part3.G
  N14: Part1.VBAT, Part2.VBAT, Part3.VBAT
  N15: Part1.EN, Part2.EN, Part3.EN
  N16: Part1.USB, Part2.VBUS, Part3.USB, Part4.USB, Part4.N$72, Part4.N$126, J1.pin3
  N17: Part1.N, Part2.D13, Part3.N
  N18: Part1.M, Part2.D12, Part3.M
  N19: Part1.L, Part2.D11, Part3.L
  N20: Part1.K, Part2.D10, Part3.K
  N21: Part1.J, Part2.D9, Part3.J
  N22: Part1.I, Part2.D6, Part3.I
  N23: Part1.H, Part2.D5, Part3.H
  N24: Part1.SCL, Part2.SCL, Part3.SCL
  N25: Part1.SDA, Part2.SDA, Part3.SDA
  N26: Part4.M, Part4.N$128, J1.pin1
  N27: Part4.GND, Part4.N$127, J1.pin2
  N28: Part4.N$91, Part4.N$96

custom parts:
  Adafruit 3.5in 480x320 TFT FeatherWing: Spice up your Feather project with a beautiful 3.5" touchscreen display shield with built in microSD card socket. This TFT display is 3.5" diagonal with a bright 6 white-LED backlight. You get a massive 480x320 pixels with individual 16-bit color pixel control. It has way more resolution than a black and white 128x64 display, and twice as much as our 2.4" TFT FeatherWing. As a bonus, this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
  Adafruit ESP32-S3 Feather: The ESP32-S3 has arrived in Feather format - and what a great way to get started with this powerful new chip from Espressif! With dual 240 MHz cores, WiFi and BLE support, and native USB, this Feather is great for powering your IoT projects. That's right - it's the new Adafruit ESP32-S3 Feather! With native USB and 8 MB flash, this board will let you upgrade your existing ESP32 projects.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
  Adafruit DC+Stepper FeatherWing: This is the DC Motor + Stepper FeatherWing which will let you use 2 x bi-polar stepper motors or 4 x brushed DC motorx (or 1 stepper and 2 DC motors). Using our Feather Stacking Headers or Feather Female Headers you can connect a FeatherWing on top or bottom of your Feather board and let the board take flight! The original Adafruit Motorshield Kit is one of our most beloved kits, which is why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
  Adafruit FeatherWing Proto: This is the FeatherWing Proto - a prototyping add-on for all Feather boards. Using our Feather Stacking Headers or Feather Female Headers you can connect a FeatherWing on top or bottom of your Feather board and let the board take flight! This has a duplicate breakout for each pin on a Feather, as well as a bunch of plain grid proto holes. For GND and 3.3V, we give you a strip of connected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
