# Fritzing sketch ServoHAT (saved by Fritzing 0.9.6b)

parts:
  Part1 = Adafruit DC+Stepper Motor HAT [part_number="Adafruit #2348"]
  M1 = Stepper Motor - Bipolar
  M2 = Stepper Motor - Bipolar
  Part2 = Adafruit DS1307 RTC Breakout [part_number="Adafruit #264"]
  Part3 = Adafruit NAU7802
  J1 = Screw terminal - 2 pins [package=THT]

nets:
  N1: Part1.SDA, Part1.N$49, Part1.N$78, Part2.SDA, Part3.SDA
  N2: Part1.SCL, Part1.N$46, Part1.N$81, Part2.SCL, Part3.SCL
  Power Fail\: Part1.GPIO5, Part1.N$13, J1.pin2
  N3: Part1.M2A, M1.A
  N4: Part1.M2B, M1.C
  N5: Part1.M1B, M1.B
  N6: Part1.M1A, M1.D
  N7: Part1.M4A, M2.A
  N8: Part1.M4B, M2.C
  N9: Part1.M3B, M2.B
  N10: Part1.M3A, M2.D
  N11: Part1.5.0V, Part1.N$73, Part2.VCC
  3.3V: Part1.3.3V, Part1.N$33, Part3.VCC
  GND: Part1.GND, Part1.N$5, Part1.N$41, Part1.N$70, Part2.GND, Part3.GND, J1.pin1
  N12: Part1.N$32, Part1.N$38, Part3.AVDD
  N13: Part1.N$54, Part3.DRDY
  N14: Part1.N$86, Part2.SQW

custom parts:
  Adafruit DC+Stepper Motor HAT: Let your robotic dreams come true with the new DC+Stepper Motor HAT from Adafruit. This Raspberry Pi add-on is perfect for any motion project as it can drive up to 4 DC or 2 Stepper motors with full PWM speed control. Since the Raspberry Pi does not have a lot of PWM pins, we use a fully-dedicated PWM driver chip onboard to both control motor direction and speed. This chip handles all the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
  Adafruit DS1307 RTC Breakout: This is a great battery-backed real time clock (RTC) that allows your microcontroller project to keep track of time even if it is reprogrammed, or if the power is lost. Perfect for datalogging, clock-building, time stamping, timers and alarms, etc. The DS1307 is the most popular RTC - but it requires 5V power to work (although we've used it with 5V power and 3.3V logic successfully) PCB &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
